# Fritzing sketch spires (saved by Fritzing 1.0.3b)
circuit board: 5.7cm x 6.1cm
breadboards: 2

parts:
  Nano = Arduino Nano (Rev3.0)
  RE1 = Rotary Encoder [package=THT]
  S5 = SPST Switch [package=switch-spdt_kit]
  A1 = VL53lox  # not connected
  U1 = AD9833 Module  # not connected
  A2 = VL53lox  # not connected
  J5 = 3.5mm Audio Jack-wq-pj320b.fzpz [package=audio-jack-3.5mm-smd]  # not connected
  J6 = 3.5mm Audio Jack-wq-pj320b.fzpz [package=audio-jack-3.5mm-smd]  # not connected
  VCC1 = 4 x AAA Battery Mount
  LDR5 = Photocell (LDR) [power=0.25W dark_resistance_@0.01lx=300kΩ light_resistance_@100lx=400Ω luminance=10lx package=THT]  # not connected
  LED8 = LED - 3mm [color="Red (635nm)" current=0.030A package="3 mm [THT]"]  # not connected
  1K2 = Resistor [tolerance=±5% resistance=1k power=0.25W package=THT]  # not connected

nets:
  GND: Nano.GND, RE1.GND, RE1.SW-2
  N1: Nano.D4, RE1.SW-1
  N2: Nano.D5, RE1.Pin-B
  N3: Nano.D6, RE1.Pin-A
  N4: Nano.VIN, S5.S
  V++: Nano.5V
  N5: S5.P, VCC1.+

notes:
  blueprint@poetaster.de 2025
  spires v1

custom parts:
  Rotary Encoder: Rotary Encoder with push button
  VL53lox: VL53L0X Time-of-Flight (ToF) Laser Ranging Sensor Breakout.
  AD9833 Module: programmable waveform generator
  3.5mm Audio Jack-wq-pj320b.fzpz: 3.5mm Audio Jack WQP-PJ320B is a SMD jack, dia 1/8 inch, female, right angle and through hole.
  4 x AAA Battery Mount: A 4 x AAA battery pack (4.8 Volts with recharables)
